# Fritzing sketch fz_sema (saved by Fritzing 0.9.3b)
breadboards: 1

parts:
  KY-1 = Keyes Relay [package=THT]
  KY-2 = Keyes Relay [package=THT]
  DHT11_1 = DHT11 module
  MH-Real-Time_Clock_Module_4 = RTC_DS1302_module
  YF-S201_Flow_Meter3 = YF-S201 Water Flow Meter
  부품5 = FC-28 Soil Hygrometer Module - Probe
  Load_Cell3 = Load Cell - Red/white/black/green
  Part3 = HX711 Weighing Sensor Module
  부품6 = FC-28 Soil Hygrometer Module
  M1 = DOIT Esp32 DevKit v1 (30 pins long, 11 pins width) [part_number=ESP32S-PIN30]
  U1 = Nokia 6100 Color LCD [package=nokia6100_lcd]
  VALVE1 = Plastic Solenoid Valve
  M2 = DC Motor

nets:
  N1: KY-1.signal, M1.D26
  N2: KY-1.NC, VALVE1.no_name_yet#1
  N3: KY-1.C, VALVE1.no_name_yet#2
  N4: KY-2.signal, M1.D33
  N5: KY-2.NC, M2.pin_1
  N6: KY-2.C, M2.pin_2
  N7: DHT11_1.DATA, M1.D25
  N8: MH-Real-Time_Clock_Module_4.RST, Part3.DO/RX, M1.D22, M1.D14
  N9: MH-Real-Time_Clock_Module_4.DAT, M1.D12
  N10: MH-Real-Time_Clock_Module_4.CLK, M1.D13
  N11: YF-S201_Flow_Meter3.SIG, M1.D27
  N12: 부품5.POS, 부품6.POS
  N13: 부품5.NEG, 부품6.NEG
  N14: Load_Cell3.wire1, Part3.E+
  N15: Load_Cell3.wire2, Part3.E-
  N16: Load_Cell3.wire3, Part3.A+
  N17: Load_Cell3.wire4, Part3.A-
  N18: Part3.CK/TX, M1.D23
  N19: 부품6.AO, M1.D35
  N20: M1.RX2, U1.LEDGND
  N21: M1.TX2, U1.GND

custom parts:
  Keyes Relay: The Keyes 5V relay module is suitable for SCM development, home appliance control. It uses a 5V~12V TIL control signal which can control DC / AC signal.
  DHT11 module: DHT11 black pcb module
  RTC_DS1302_module: Arduino module DS1302 SPI Real Time Clock
  YF-S201 Water Flow Meter: The YF-S201 Flow Meter. The input voltage is 5V to 24V (DC).
  FC-28 Soil Hygrometer Module - Probe: The FC-28 is a soil hygrometer module that uses the Texas Instruments LM393 comparator chip to provide an analog measurement of soil humidity.
  Load Cell - Red/white/black/green: A rectangle load cell/weighting pressure Sensor with four wires - Red, white, black, green. Normally corresponding with E+, E-, A+, A- respectively.
  HX711 Weighing Sensor Module: HX711 is a precision 24-bit analog-to-digital converter (ADC) designed for weigh scales and industrial control applications to interface directly with a bridge sensor.
  FC-28 Soil Hygrometer Module: The FC-28 is a soil hygrometer module that uses the Texas Instruments LM393 comparator chip to provide an analog measurement of soil humidity. The digital output is high when soil moisture is over a certain threshold, as determined by adjusting the potentiometer.
  DOIT Esp32 DevKit v1 (30 pins long, 11 pins width): The DOIT Esp32 DevKit v1 is one of the development board created by DOIT to evaluate the ESP-WROOM-32 module. It is based on the ESP32 microcontroller that boasts Wifi, Bluetooth, Ethernet and Low Power support all in a single chip. (vanepp) made breadboard work, adjusted pin numbering and labels and reduced size of schematic and cleaned up pcb. This chip is 30pins long (2 x15) and 11 pins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
